# Fritzing sketch circuit (saved by Fritzing 0.9.4)

parts:
  U1 = 74LS74-Flipflops [part_number=74LS74 package="DIP (Dual Inline) [THT]"]  # not connected
  Bauteil3 = 74LS74-Flipflops [part_number=74LS74 package="DIP (Dual Inline) [THT]"]
  U1_1 = 74LS74-Flipflops [part_number=74LS74 package="DIP (Dual Inline) [THT]"]
  U1_2 = 74LS74-Flipflops [part_number=74LS74 package="DIP (Dual Inline) [THT]"]
  Bauteil1 = Adafruit Micro USB Breakout [part_number="Adafruit #1833"]
  R1 = Resistor [tolerance=±5% resistance=10k package="0402 [SMD]"]
  R2 = Resistor [tolerance=±5% resistance=100k package="0402 [SMD]"]
  Bauteil2 = Adafruit TPL5110 Power Timer [part_number="Adafruit #3435"]
  R3 = Resistor [tolerance=±5% resistance=180k package="0402 [SMD]"]
  MCU1 = Raspberry Pi Zero
  C2 = Ceramic Capacitor [capacitance=100nF package="200 mil [THT, multilayer]"]

nets:
  GND: Bauteil3.7, Bauteil1.GND, R2.Pin_0, Bauteil2.GND, R3.Pin_0, MCU1.pin_20, MCU1.pin_39, C2.0
  N1: Bauteil3.14, U1_1.2, U1_1.4, U1_2.10, R1.Pin_1, Bauteil2.PWROUT, MCU1.pin_4
  N2: U1_1.1, U1_2.13, R1.Pin_0, R2.Pin_1, C2.1
  N3: U1_1.3, U1_2.11, MCU1.pin_32
  N4: U1_1.5, U1_2.12
  N5: U1_2.9, Bauteil2.DONE
  N6: Bauteil2.DELAY, R3.Pin_1

custom parts:
  Adafruit Micro USB Breakout: Simple but effective - this breakout board has a USB Micro-B connector, with all 5 pins broken out. Great for pairing with a microcontroller with USB support, or adding USB 5V power to a project. We use a micro-AB connector with through-hole shielding pads for an excellent strong connection - it won't rip off by accident! Comes with one fully assembled and tested micro B breakout PCB and a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
  Adafruit TPL5110 Power Timer: With some development boards, low power usage is an afterthought. Especially when price and usability is the main selling point. So what should you do when its time to turn around and make that project of yours run on a battery or solar? Sure you could try to hot-air that regulator off, or you could jerry-rig a relay. Or, use a 555? Ugh, the options aren't that great. The Adafruit TPL5110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
